// Logisim project DL lab . 6.circ as structural Verilog: 1 circuit, main circuit main
module main (
  input  A,
  input  B,
  input  C,
  input  D,
  input  B_2,
  input  D_2,
  output out_7,
  output out_8
);

  wire A_prime_out, and_1_out, and_2_out, and_3_out, and_4_out, and_5_out, and_6_out, and_7_out, and_8_out,
       and_9_out, and_10_out, B_prime_2_out, B_prime_out, C_prime_out, D_prime_2_out, D_prime_out;

  not A_prime (A_prime_out, A);
  not B_prime (B_prime_out, B);
  not C_prime (C_prime_out, C);
  not D_prime (D_prime_out, D);
  and and_1 (and_1_out, A_prime_out, B_prime_out, C_prime_out, D_prime_out);
  and and_2 (and_2_out, A_prime_out, B_prime_out, C, D_prime_out);
  and and_3 (and_3_out, A_prime_out, B, C_prime_out, D);
  and and_4 (and_4_out, A_prime_out, B, C, D);
  and and_5 (and_5_out, A, B_prime_out, C_prime_out, D_prime_out);
  and and_6 (and_6_out, A, B_prime_out, C, D_prime_out);
  and and_7 (and_7_out, A, B, C_prime_out, D);
  and and_8 (and_8_out, A, B, C, D);
  or or_1 (out_7, and_1_out, and_2_out, and_3_out, and_4_out, and_5_out, and_6_out, and_7_out, and_8_out);
  not B_prime_2 (B_prime_2_out, B_2);
  not D_prime_2 (D_prime_2_out, D_2);
  and and_9 (and_9_out, B_prime_2_out, D_prime_2_out);
  and and_10 (and_10_out, B_2, D_2);
  or or_2 (out_8, and_9_out, and_10_out);
endmodule
