// Logisim project DL lab .1.circ as structural Verilog: 1 circuit, main circuit main
module main (
  input  A,
  input  B,
  input  A_2,
  input  B_2,
  input  A_3,
  input  A_4,
  input  B_3,
  input  A_5,
  input  B_4,
  output out_10,
  output out_11,
  output out_12,
  output out_13,
  output out_14
);

  and and_1 (out_10, A, B);
  or or_1 (out_11, A_2, B_2);
  not not_1 (out_12, A_3);
  xor xor_1 (out_13, A_4, B_3);
  xnor xnor_1 (out_14, A_5, B_4);
endmodule
