// Logisim project DL lab .10.circ as structural Verilog: 1 circuit, main circuit main
module main (
  input  A,
  input  B,
  input  BIN,
  output DIFFERENCE,
  output B0UT
);

  wire and_1_out, and_2_out, not_1_out, not_2_out, xor_1_out;

  xor xor_1 (xor_1_out, A, B);
  not not_1 (not_1_out, xor_1_out);
  not not_2 (not_2_out, A);
  xor xor_2 (DIFFERENCE, xor_1_out, BIN);
  and and_1 (and_1_out, not_1_out, BIN);
  and and_2 (and_2_out, not_2_out, B);
  or or_1 (B0UT, and_1_out, and_2_out);
endmodule
