// Logisim project DL lab .2.circ as structural Verilog: 1 circuit, main circuit main
module main (
  input  in_1,
  input  in_2,
  input  in_3,
  input  in_4,
  input  in_5,
  input  in_6,
  input  in_7,
  input  in_8,
  output out_9,
  output out_10,
  output out_11
);

  wire nand_2_out, nand_3_out, nand_4_out;

  nand nand_1 (out_9, in_1, in_2);
  nand nand_2 (nand_2_out, in_3, in_4);
  nand nand_3 (nand_3_out, in_5, in_6);
  nand nand_4 (nand_4_out, in_7, in_8);
  nand nand_5 (out_10, nand_2_out, nand_2_out);
  nand nand_6 (out_11, nand_3_out, nand_4_out);
endmodule
