// Logisim project DL lab .8.circ as structural Verilog: 1 circuit, main circuit main
module main (
  input  A,
  input  B,
  input  cin,
  output sum,
  output carry
);

  wire and_1_out, and_2_out, xor_1_out;

  xor xor_1 (xor_1_out, A, cin);
  xor xor_2 (sum, xor_1_out, cin);
  and and_1 (and_1_out, xor_1_out, cin);
  and and_2 (and_2_out, A, B);
  or or_1 (carry, and_1_out, and_2_out);
endmodule
