// Logisim project DL lab .9.circ as structural Verilog: 1 circuit, main circuit main
module main (
  input  in_1,
  input  in_2,
  output difference,
  output borrow
);

  wire not_1_out;

  not not_1 (not_1_out, in_1);
  xor xor_1 (difference, in_1, in_2);
  and and_1 (borrow, not_1_out, in_2);
endmodule
